# Fritzing sketch iotress6 (saved by Fritzing 0.9.3b)
circuit board: 8.46667cm x 5.64444cm
breadboards: 1

parts:
  Power_plug = Power plug
  button = Round Pushbutton
  R1 = Resistor [tolerance=±5% resistance=220 package=THT]
  R2 = Resistor [tolerance=±5% resistance=330 package=THT]
  R3 = Resistor [tolerance=±5% resistance=220 package=THT]
  R4 = Resistor [tolerance=±5% resistance=330 package=THT]
  R6 = Resistor [tolerance=±5% resistance=330 package=THT]
  sdcs = female pin header, 1 pin [form="♀ (female)"]
  com4 = male pin header, 1 pin [form="♂ (male)"]
  com11 = male pin header, 1 pin [form="♂ (male)"]
  com8 = male pin header, 1 pin [form="♂ (male)"]
  mosi = female pin header, 1 pin [form="♀ (female)"]
  sck = female pin header, 1 pin [form="♀ (female)"]
  comA0 = male pin header, 1 pin [form="♂ (male)"]
  LED1 = LED - 5mm [color="Red (633nm)" package="5 mm [THT]"]
  LED2 = LED - 5mm [color="Green (565nm)" package="5 mm [THT]"]
  POTEN = Rotary Potentiometer (Large) [maximum_resistance=10kΩ package=THT]
  R13 = Resistor [tolerance=±5% resistance=220 package=THT]
  R14 = Resistor [tolerance=±5% resistance=220 package=THT]
  com9 = male pin header, 1 pin [form="♂ (male)"]
  com13 = male pin header, 1 pin [form="♂ (male)"]
  R5 = Resistor [tolerance=±5% resistance=220 package=THT]
  scl_sda_vcc_gnd = female pin header, 4 pins [form="♀ (female)"]
  com_5_com_4 = male pin header, 2 pins [form="♂ (male)"]
  miso_gnd_vcc = female pin header, 3 pins [form="♀ (female)"]
  com_12_gnd_vcc = male pin header, 3 pins [form="♂ (male)"]

nets:
  GND/gnd_sdcard: Power_plug.GND, R2.Pin_1, R4.Pin_1, R6.Pin_1, POTEN.wiper, R13.Pin_1, R14.Pin_1, scl_sda_vcc_gnd.pin4, miso_gnd_vcc.pin2, com_12_gnd_vcc.pin2
  N1: Power_plug.VCC, button.leg1
  5V/button L: button.leg0, POTEN.leg2, scl_sda_vcc_gnd.pin3, miso_gnd_vcc.pin3, com_12_gnd_vcc.pin3
  N2: R1.Pin_0, com4.pin1
  N3: R1.Pin_1, R2.Pin_0, sdcs.pin1
  N4: R3.Pin_0, com11.pin1
  N5: R3.Pin_1, R4.Pin_0, mosi.pin1
  N6: R6.Pin_0, sck.pin1, R5.Pin_1
  N7: com8.pin1, R5.Pin_0
  N8: comA0.pin1, POTEN.leg1
  N9: LED1.cathode, R13.Pin_0
  N10: LED1.anode, com13.pin1
  N11: LED2.cathode, R14.Pin_0
  N12: LED2.anode, com9.pin1
  scl: scl_sda_vcc_gnd.pin1, com_5_com_4.pin1
  sda: scl_sda_vcc_gnd.pin2, com_5_com_4.pin2
  MISO: miso_gnd_vcc.pin1, com_12_gnd_vcc.pin1
